# Fritzing sketch Схема (saved by Fritzing 0.9.4)

parts:
  U1 = ESP8266 WiFi Module [part_number=ESP8266]
  DHT1 = DHT22 Humidity and Temperature Sensor
  VCC1 = Battery
  S1 = Pushbutton [package=THT]

nets:
  VCC: U1.VCC, DHT1.VDD, VCC1.+
  GND: U1.GND, DHT1.GND, VCC1.-, S1.leg0
  N1: U1.GPIO_5, DHT1.DATA
  N2: U1.GPIO_16, U1.REST, S1.leg1
